# Fritzing sketch firtziz (saved by Fritzing 0.9.3b)
breadboards: 1

parts:
  LED1 = smd LED [color="Red (633nm)" package="1206 [SMD]"]
  LED7 = smd LED [color="Red (633nm)" package="1206 [SMD]"]
  LED9 = smd LED [color="Red (633nm)" package="1206 [SMD]"]
  LED10 = smd LED [color="Red (633nm)" package="1206 [SMD]"]
  LED11 = smd LED [color="Red (633nm)" package="1206 [SMD]"]
  LED12 = smd LED [color="Red (633nm)" package="1206 [SMD]"]
  LED13 = smd LED [color="Red (633nm)" package="1206 [SMD]"]
  LED14 = smd LED [color="Red (633nm)" package="1206 [SMD]"]
  LED15 = smd LED [color="Red (633nm)" package="1206 [SMD]"]
  LED16 = smd LED [color="Red (633nm)" package="1206 [SMD]"]
  R1 = Resistor [tolerance=±5% resistance=220 package=THT]
  R2 = Resistor [tolerance=±5% resistance=220 package=THT]
  R3 = Resistor [tolerance=±5% resistance=220 package=THT]
  R4 = Resistor [tolerance=±5% resistance=220 package=THT]
  R5 = Resistor [tolerance=±5% resistance=220 package=THT]
  R6 = Resistor [tolerance=±5% resistance=220 package=THT]
  R7 = Resistor [tolerance=±5% resistance=220 package=THT]
  R8 = Resistor [tolerance=±5% resistance=220 package=THT]
  R9 = Resistor [tolerance=±5% resistance=220 package=THT]
  R10 = Resistor [tolerance=±5% resistance=220 package=THT]
  Composant1 = Arduino Uno (Rev3)

nets:
  N1: LED1.cathode, Composant1.D7
  N2: LED1.anode, R1.Pin_1
  N3: LED7.cathode, Composant1.D4
  N4: LED7.anode, R4.Pin_0
  N5: LED9.cathode, Composant1.D5_PWM
  N6: LED9.anode, R3.Pin_0
  N7: LED10.cathode, Composant1.D6_PWM
  N8: LED10.anode, R2.Pin_0
  N9: LED11.cathode, Composant1.D3_PWM
  N10: LED11.anode, R5.Pin_0
  N11: LED12.cathode, Composant1.D2
  N12: LED12.anode, R6.Pin_0
  N13: LED13.cathode, Composant1.D10_PWM/SS
  N14: LED13.anode, R7.Pin_1
  N15: LED14.cathode, R8.Pin_1, Composant1.D9_PWM
  N16: LED15.cathode, Composant1.D8
  N17: LED15.anode, R10.Pin_1
  N18: LED16.anode, R9.Pin_1
  N19: R1.Pin_0, R2.Pin_1, R3.Pin_1, R4.Pin_1, R5.Pin_1, R6.Pin_1, R8.Pin_0, R9.Pin_0, R10.Pin_0, Composant1.GND
